// Logisim project lista-2.circ as structural Verilog: 4 circuits, main circuit meio somador
module meio_somador (
  input  A,
  input  B,
  output Carry,
  output Soma
);

  and and_1 (Carry, B, A);
  xor xor_1 (Soma, A, B);
endmodule

module somador_completo (
  input  Carry_anterior,
  input  A,
  input  B,
  output Carry,
  output Soma
);

  wire and_1_out, and_2_out, xor_1_out;

  and and_1 (and_1_out, B, A);
  xor xor_1 (xor_1_out, A, B);
  and and_2 (and_2_out, Carry_anterior, xor_1_out);
  or or_1 (Carry, and_1_out, and_2_out);
  xor xor_2 (Soma, Carry_anterior, xor_1_out);
endmodule

module somador_4_bits (
  input  in_1,
  input  in_2,
  input  in_3,
  input  in_4,
  output out_5,
  output out_6,
  output out_7
);

  wire meio_somador_1_carry;

  somador_completo somador_completo_1 (
    .Carry_anterior(meio_somador_1_carry), .A(in_2), .B(in_4), .Carry(out_5), .Soma(out_6));
  meio_somador meio_somador_1 (.A(in_1), .B(in_3), .Carry(meio_somador_1_carry), .Soma(out_7));
endmodule

module sla (
  input  A,
  input  B,
  input  C,
  input  D,
  output Carry1,
  output Carry2,
  output Soma
);

  wire adder_1_cout;

  Adder #(.width(1)) adder_1 (.a(A), .b(B), .out(Carry1), .cout(adder_1_cout));  // open: cin
  Adder #(.width(1)) adder_2 (.a(C), .b(D), .out(Soma), .cin(adder_1_cout), .cout(Carry2));
endmodule
