// Logisim project aritimeticos.circ as structural Verilog: 11 circuits, main circuit meio somador
module meio_somador (
  input  A,
  input  B,
  output Carry,
  output Soma
);

  and and_1 (Carry, B, A);
  xor xor_1 (Soma, A, B);
endmodule

module somador_completo (
  input  Carry_anterior,
  input  A,
  input  B,
  output Carry,
  output Soma
);

  wire and_1_out, and_2_out, xor_1_out;

  and and_1 (and_1_out, B, A);
  xor xor_1 (xor_1_out, A, B);
  and and_2 (and_2_out, Carry_anterior, xor_1_out);
  or or_1 (Carry, and_1_out, and_2_out);
  xor xor_2 (Soma, Carry_anterior, xor_1_out);
endmodule

module somador_2_bits (
  input  A0,
  input  B0,
  input  _1A,
  input  _1B,
  output Digito_3,
  output Digito_2,
  output Digito_1
);

  wire meio_somador_1_carry;

  meio_somador meio_somador_1 (.A(A0), .B(B0), .Carry(meio_somador_1_carry), .Soma(Digito_1));
  somador_completo somador_completo_1 (
    .Carry_anterior(meio_somador_1_carry), .A(_1A), .B(_1B), .Carry(Digito_3), .Soma(Digito_2));
endmodule

module Somador_4_bits_individuais_logisim (
  input  in_1,
  input  in_2,
  input  in_3,
  input  in_4,
  input  in_5,
  input  in_6,
  input  in_7,
  input  in_8,
  output out_9,
  output out_10,
  output out_11,
  output out_12,
  output out_13
);

  wire adder_1_cout, adder_2_cout, adder_3_cout;

  Adder #(.width(1)) adder_1 (.a(in_1), .b(in_2), .out(out_13), .cout(adder_1_cout));  // open: cin
  Adder #(.width(1)) adder_2 (.a(in_3), .b(in_4), .out(out_12), .cin(adder_1_cout), .cout(adder_2_cout));
  Adder #(.width(1)) adder_3 (.a(in_5), .b(in_6), .out(out_11), .cin(adder_2_cout), .cout(adder_3_cout));
  Adder #(.width(1)) adder_4 (.a(in_7), .b(in_8), .out(out_10), .cin(adder_3_cout), .cout(out_9));
endmodule

module somador_4_bits_logisim (
  input  [3:0] in_1,
  input  [3:0] in_2,
  output [3:0] out_3,
  output out_4
);

  Adder #(.width(4)) adder_1 (.a(in_1), .b(in_2), .out(out_3), .cout(out_4));  // open: cin
endmodule

module somador_com_2_somadores_de_4_bits (
  input  [3:0] in_1,
  input  [3:0] in_2,
  input  [3:0] in_3,
  input  [3:0] in_4,
  output out_5,
  output [3:0] out_6,
  output [3:0] out_7
);

  wire adder_1_cout;

  Adder #(.width(4)) adder_1 (.a(in_1), .b(in_2), .out(out_7), .cout(adder_1_cout));  // open: cin
  Adder #(.width(4)) adder_2 (.a(in_3), .b(in_4), .out(out_6), .cin(adder_1_cout), .cout(out_5));
endmodule

module subtrator_4_bits (
  input  [3:0] in_1,
  input  [3:0] in_2,
  output [3:0] out_3,
  output out_4
);

  Subtractor #(.width(4)) subtractor_1 (.a(in_1), .b(in_2), .out(out_3), .bout(out_4));  // open: bin
endmodule

module negador_4_bits (
  input  [3:0] in_1,
  output [3:0] out_2
);

  Negator #(.width(4)) negator_1 (.in(in_1), .out(out_2));
endmodule

module subtrator_4_bits_com_negador_e_somador (
  input  [3:0] in_1,
  input  [3:0] in_2,
  output [3:0] out_3
);

  wire [3:0] negator_1_out;

  Negator #(.width(4)) negator_1 (.in(in_2), .out(negator_1_out));
  Adder #(.width(4)) adder_1 (.a(in_1), .b(negator_1_out), .out(out_3));  // open: cin, cout
endmodule

module multiplicador_4_bits (
  input  [3:0] _4_bits,
  input  [3:0] in_2,
  output [3:0] out_3,
  output [3:0] out_4
);

  Multiplier #(.width(4)) multiplier_1 (.a(_4_bits), .b(in_2), .out(out_3), .cout(out_4));  // open: cin

  // Notes on the sheet:
  //   8 bits
endmodule

module comparador_4_bits (
  input  [3:0] in_1,
  input  [3:0] in_2,
  output out_3,
  output out_4,
  output out_5
);

  Comparator #(.width(4)) comparator_1 (.a(in_1), .b(in_2), .gt(out_3), .eq(out_4), .lt(out_5));
endmodule
