// Logisim project memorias.circ as structural Verilog: 1 circuit, main circuit main
module main (
  input  [3:0] \Endereço ,
  input  [7:0] Entrada,
  input  Escrita,
  input  \Seleção_de_memória ,
  input  Clock,
  input  Leitura,
  input  Limpar,
  output [7:0] \Saída 
);

  RAM #(.addrWidth(4), .bus("separate")) ram_1 (
    .addr(\Endereço ), .din(Entrada), .data(\Saída ), .str(Escrita), .sel(\Seleção_de_memória ), .clk(Clock),
    .ld(Leitura), .clr(Limpar));
endmodule
