// Logisim project exercicio-2.circ as structural Verilog: 1 circuit, main circuit main
module main (
  input  A,
  input  B,
  input  C,
  output S
);

  wire and_1_out, and_2_out, and_3_out, not_1_out, not_2_out;

  not not_1 (not_1_out, A);
  and and_1 (and_1_out, A, C);
  and and_2 (and_2_out, B, C);
  and and_3 (and_3_out, not_1_out, C, B);
  not not_2 (not_2_out, and_2_out);
  or or_1 (S, and_1_out, not_2_out, and_3_out);

  // Notes on the sheet:
  //   exercicio 2
endmodule
