// Logisim project lista-3.circ as structural Verilog: 5 circuits, main circuit decodificadores 1
module decodificadores_1 (
  input  in_1,
  input  in_2,
  output out_3,
  output out_4,
  output out_5,
  output out_6
);

  wire not_1_out, not_2_out, not_3_out, not_4_out;

  not not_1 (not_1_out, in_2);
  not not_2 (not_2_out, in_1);
  not not_3 (not_3_out, in_1);
  not not_4 (not_4_out, in_2);
  and and_1 (out_3, not_1_out, not_2_out);
  and and_2 (out_4, in_2, not_3_out);
  and and_3 (out_5, not_4_out, in_1);
  and and_4 (out_6, in_2, in_1);
endmodule

module decodificadores_2 (
  input  in_1,
  input  in_2,
  input  in_3,
  output out_4,
  output out_5,
  output out_6,
  output out_7,
  output out_8,
  output out_9,
  output out_10,
  output out_11
);

  wire and_1_out, and_2_out, and_3_out, and_4_out, and_5_out, and_6_out, and_7_out, and_8_out, not_1_out,
       not_2_out, not_3_out, not_4_out, not_5_out, not_6_out, not_7_out, not_8_out, not_9_out, not_10_out,
       not_11_out, not_12_out;

  not not_1 (not_1_out, in_3);
  not not_2 (not_2_out, in_2);
  not not_3 (not_3_out, in_2);
  not not_4 (not_4_out, in_3);
  not not_5 (not_5_out, in_3);
  not not_6 (not_6_out, in_2);
  not not_7 (not_7_out, in_2);
  not not_8 (not_8_out, in_3);
  and and_1 (and_1_out, not_1_out, not_2_out);
  not not_9 (not_9_out, in_1);
  and and_2 (and_2_out, in_3, not_3_out);
  not not_10 (not_10_out, in_1);
  and and_3 (and_3_out, not_4_out, in_2);
  not not_11 (not_11_out, in_1);
  and and_4 (and_4_out, not_5_out, not_6_out);
  and and_5 (and_5_out, in_3, in_2);
  not not_12 (not_12_out, in_1);
  and and_6 (and_6_out, in_3, not_7_out);
  and and_7 (and_7_out, not_8_out, in_2);
  and and_8 (and_8_out, in_3, in_2);
  and and_9 (out_4, and_1_out, not_9_out);
  and and_10 (out_5, and_2_out, not_10_out);
  and and_11 (out_6, and_3_out, not_11_out);
  and and_12 (out_7, and_4_out, in_1);
  and and_13 (out_8, and_5_out, not_12_out);
  and and_14 (out_9, and_6_out, in_1);
  and and_15 (out_10, and_7_out, in_1);
  and and_16 (out_11, and_8_out, in_1);
endmodule

module decodificadores_3 (
  input  [1:0] in_1,
  output out_2,
  output out_3,
  output out_4,
  output out_5
);

  Decoder #(.select(2)) decoder_1 (.out0(out_2), .out1(out_3), .out2(out_4), .out3(out_5), .sel(in_1));  // open: en
endmodule

module decodificadores_4 (
  input  [2:0] in_1,
  output out_2,
  output out_3,
  output out_4,
  output out_5,
  output out_6,
  output out_7,
  output out_8,
  output out_9
);

  Decoder #(.select(3)) decoder_1 (
    .out0(out_2), .out1(out_3), .out2(out_4), .out3(out_5), .out4(out_6), .out5(out_7), .out6(out_8),
    .out7(out_9), .sel(in_1));  // open: en
endmodule

module \memórias_1  (
  input  [3:0] \Endereço ,
  input  [7:0] Entrada,
  input  Escrita,
  input  \Seleção_de_memória ,
  input  Clock,
  input  Leitura,
  input  Limpar,
  output [7:0] \Saída 
);

  RAM #(.addrWidth(4), .bus("separate")) ram_1 (
    .addr(\Endereço ), .din(Entrada), .data(\Saída ), .str(Escrita), .sel(\Seleção_de_memória ), .clk(Clock),
    .ld(Leitura), .clr(Limpar));
endmodule
