// Logisim project clock.circ as structural Verilog: 1 circuit, main circuit main
module main (
  output [3:0] out_1,
  output [3:0] out_2,
  output [3:0] out_3,
  output [3:0] out_4,
  output [3:0] out_5,
  output [3:0] out_6,
  output out_7
);

  wire clock_1_out, counter_1_carry, counter_2_carry, counter_3_carry, counter_4_carry, counter_5_carry,
       counter_6_carry;

  Hex_Digit_Display hex_digit_display_1 (.value(out_2));  // open: dp
  Hex_Digit_Display hex_digit_display_2 (.value(out_1));  // open: dp
  Counter #(.width(4), .max('h9), .trigger("falling")) counter_1 (
    .Q(out_5), .carry(counter_1_carry), .clk(clock_1_out), .clr(counter_6_carry));  // open: load, D, count
  Clock clock_1 (.out(clock_1_out));
  Hex_Digit_Display hex_digit_display_3 (.value(out_3));  // open: dp
  Hex_Digit_Display hex_digit_display_4 (.value(out_4));  // open: dp
  Hex_Digit_Display hex_digit_display_5 (.value(out_6));  // open: dp
  Counter #(.width(4), .max('h5), .trigger("falling")) counter_2 (
    .Q(out_6), .carry(counter_2_carry), .clk(counter_1_carry), .clr(counter_6_carry));  // open: load, D, count
  Hex_Digit_Display hex_digit_display_6 (.value(out_5));  // open: dp
  Counter #(.width(4), .max('h9), .trigger("falling")) counter_3 (
    .Q(out_3), .carry(counter_3_carry), .clk(counter_2_carry), .clr(counter_6_carry));  // open: load, D, count
  Counter #(.width(4), .max('h5), .trigger("falling")) counter_4 (
    .Q(out_4), .carry(counter_4_carry), .clk(counter_3_carry), .clr(counter_6_carry));  // open: load, D, count
  Counter #(.width(4), .max('h9), .trigger("falling")) counter_5 (
    .Q(out_1), .carry(counter_5_carry), .clk(counter_4_carry), .clr(counter_6_carry));  // open: load, D, count
  Counter #(.width(5), .max('h18), .trigger("falling")) counter_6 (
    .carry(counter_6_carry), .clk(counter_4_carry));  // open: load, D, count, Q, clr
  Counter #(.width(4), .max('h2), .trigger("falling")) counter_7 (
    .Q(out_2), .carry(out_7), .clk(counter_5_carry), .clr(counter_6_carry));  // open: load, D, count
endmodule
