// Logisim project lista-1.circ as structural Verilog: 5 circuits, main circuit exercicio-1
module exercicio_1 (
  input  A,
  input  B,
  input  C,
  output S
);

  wire not_1_out, or_1_out, or_2_out;

  or or_1 (or_1_out, A, B);
  not not_1 (not_1_out, B);
  or or_2 (or_2_out, not_1_out, C);
  and and_1 (S, or_1_out, or_2_out);
endmodule

module exercicio_2 (
  input  A,
  input  C,
  input  B,
  output S
);

  wire and_1_out, and_2_out, and_3_out, not_1_out, not_2_out;

  not not_1 (not_1_out, A);
  and and_1 (and_1_out, A, C);
  and and_2 (and_2_out, C, B);
  not not_2 (not_2_out, and_2_out);
  and and_3 (and_3_out, not_1_out, C, B);
  or or_1 (S, and_1_out, not_2_out, and_3_out);
endmodule

module exercicio_3 (
  input  A,
  input  B,
  input  C,
  input  D,
  output S
);

  wire and_1_out, and_2_out, not_1_out, not_2_out;

  and and_1 (and_1_out, A, B);
  not not_1 (not_1_out, C);
  and and_2 (and_2_out, C, D);
  not not_2 (not_2_out, and_2_out);
  or or_1 (S, and_1_out, not_1_out, not_2_out);
endmodule

module exercicio_4 (
  input  W,
  input  X,
  input  Y,
  output Z
);

  wire not_1_out, or_1_out;

  not not_1 (not_1_out, Y);
  or or_1 (or_1_out, W, not_1_out);
  and and_1 (Z, X, or_1_out);
endmodule

module exercicio_5 (
  input  A,
  input  B,
  output S
);

  wire and_1_out, and_2_out, not_1_out, not_2_out;

  not not_1 (not_1_out, A);
  not not_2 (not_2_out, B);
  and and_1 (and_1_out, not_1_out, B);
  and and_2 (and_2_out, A, not_2_out);
  or or_1 (S, and_1_out, and_2_out);
endmodule
